# Fritzing sketch cuircuitDiagram2 (saved by Fritzing 0.8.7b)
breadboards: 1

parts:
  U1 = ESP32S-HiLetgo [part_number=ESP32S-HiLetgo]
  Componente1 = Humidity Sensor - HIH-4030 Breakout
  M1 = DC Motor
  VCC1 = Battery  # not connected
  Componente2 = Logic Level Converter
  K1 = Relay [part_number=FRS1B-S package=THT]

nets:
  N1: U1.GPIO27, Componente2.TX_LV
  N2: U1.GPIO9, Componente1.OUT
  GND: U1.GPIO11, Componente1.GND, Componente2.GND, K1.COIL1
  VIN: U1.VIN, Componente1.VCC, Componente2.HV, K1.A
  N3: U1.GPIO6, Componente2.RX_LV
  N4: M1.pin_1, Componente2.TX_HV, K1.C1, K1.C2

custom parts:
  ESP32S-HiLetgo: HiLetgo ESP-WROOM-32 ESP32 ESP-32S Development Board 2.4GHz Dual-Mode WiFi + Bluetooth Dual Cores Microcontroller The ESP32 integrated with Antenna switches, RF Balun, power amplifiers, low-noise amplifiers, filters, and management modules, and the entire solution occupies the least area of PCB. 2.4 GHz Wi-Fi plus Bluetooth dual-mode chip, with TSMC Ultra-low power consumption 40nm technology,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
